# Fritzing sketch diagrama (saved by Fritzing 0.9.3b)
breadboards: 1

parts:
  Componente2 = Arduino Uno (Rev3)
  R1 = Trimmer Potentiometer [maximum_resistance=10kΩ package=THT]
  GY1 = MPU-6050 Board GY-521 [form="♀ (female)" package=THT]
  U1 = LCD-16X2 [package=lcd-16x2]
  Componente4 = Black Joystick KY-023
  R2 = Resistor [tolerance=±5% resistance=220 package=THT]
  S1 = Pushbutton [package="[THT]"]
  R3 = Resistor [tolerance=±5% resistance=10k package=THT]

nets:
  N1: Componente2.A0, Componente4.VRx
  N2: Componente2.A1, Componente4.VRy
  N3: Componente2.A4/SDA, GY1.pin4
  N4: Componente2.A5/SCL, GY1.pin3
  N5: Componente2.D12/MISO, Componente4.SW
  N6: Componente2.D13/SCK, S1.Pin_3, S1.Pin_4, R3.Pin_1
  GND: Componente2.GND, R1.leg1, GY1.pin2, U1.VSS, U1.R_W, U1.K, Componente4.GND, R3.Pin_0
  N7: Componente2.D2, U1.DB7
  N8: Componente2.D3_PWM, U1.DB6
  N9: Componente2.D4, U1.DB5
  N10: Componente2.D5_PWM, U1.DB4
  N11: Componente2.D6_PWM, U1.E
  N12: Componente2.D7, U1.RS
  5V: Componente2.5V, R1.leg2, GY1.pin1, U1.VDD, Componente4.+5V, R2.Pin_0, S1.Pin_1, S1.Pin_2
  N13: R1.wiper, U1.VO
  N14: U1.A, R2.Pin_1

custom parts:
  MPU-6050 Board GY-521: Acelerometro y Giroscopio MPU-6050 Board GY-521
  Black Joystick KY-023: Description: The joystick is a combination of 2 analoog potentiometer and a digital switch. Arduino GND --> Module pin - Arduino +5V --> Module pin +5V Arduino Analoog 0 --> Module VRx Arduino Analoog 1 --> Module VRy Arduino Digital --> Module SW Dimensions: 1" x 1.25"
